# Fritzing sketch circuitos (saved by Fritzing 0.9.9b)
breadboards: 2

parts:
  Mod1 = Raspberry Pi 4B
  Driver1 = 28BYJ-48 Driver Module [part_number=ULN2003 package=THT]
  SM1 = 28BYJ-48 Stepper Motor [part_number=28BYJ-48]
  R1 = Photocell (LDR) [package=THT]
  RHT1 = Humidity and Temperature Sensor RHT03
  T1 = LM35 Temperature Sensor [package="TO92 [THT]"]
  R2 = Resistor [tolerance=±5% power=0.25 resistance=220 package=THT]
  Q1 = NPN-Transistor [package="TO92 [THT]"]
  LED1 = LED - 5mm [color="Red (633nm)" current=0.030 package="5 mm [THT]"]
  Q2 = NPN-Transistor [package="TO92 [THT]"]
  R3 = Resistor [tolerance=±5% power=0.25 resistance=220 package=THT]
  R4 = Resistor [tolerance=±5% power=0.25 resistance=220 package=THT]
  R5 = Resistor [tolerance=±5% power=0.25 resistance=220 package=THT]
  R6 = Resistor [tolerance=±5% resistance=220 package="1206 [SMD]"]
  VCC2 = 4 x AAA Battery Mount
  U1 = Vibration Motor- ROB-08449 [package=vibe-motor-10mm]
  Q3 = NPN-Transistor [package="TO92 [THT]"]

nets:
  5V: Mod1.5V, R1.pin_1, RHT1.Vcc, T1.+Vs
  GND: Mod1.GND, RHT1.GND_2, T1.GND, Q1.E, Q2.E, R6.Pin_1, Q3.E
  N1: Mod1.GPIO4, T1.Vout
  N2: Mod1.GPIO17, R1.pin_0, R6.Pin_0
  N3: Mod1.GPIO27, RHT1.Data-signal
  N4: Mod1.GPIO22, RHT1.GND_1
  N5: Mod1.GPIO23, Q2.B
  N6: Mod1.GPIO24, Q1.B
  N7: Mod1.GPIO25, Q3.B
  N8: Driver1.GND, VCC2.-
  N9: Driver1.Vmotor, R2.Pin_0, LED1.anode, R3.Pin_0, R4.Pin_0, R5.Pin_0, VCC2.+, U1.-
  N10: Driver1.blue-pin, SM1.blue-pin
  N11: Driver1.pink-pin, SM1.pink-pin
  N12: Driver1.yellow-pin, SM1.yellow-pin
  N13: Driver1.orange-pin, SM1.orange-pin
  N14: Driver1.red-pin, SM1.red-pin
  N15: R2.Pin_1, Q2.C, R3.Pin_1, R4.Pin_1, R5.Pin_1
  N16: Q1.C, LED1.cathode
  N17: U1.+, Q3.C

custom parts:
  28BYJ-48 Driver Module: ULN2003 Driver Module for the 28BYJ-48 Unipolar Stepper Motor LED A - Blue wire - Bottom coil left LED B - Pink wire - Top coil left LED C - Yellow wire - Bottom coil right LED D - Orange wire - Top coil right Common rail - red Connector pins: blue - pink - yellow - orange - red Control pins - IN1 to IN4 Power pins - GND & Vmotor (5-12V) On/Off jumper (if removed, power to motor is cut).
  28BYJ-48 Stepper Motor: Unipolar Stepper Motor 28BYJ-48 Top coil - pink & orange Bottom coil - blue & yellow Common rail - red Connector pins: blue - pink - yellow - orange - red
